# Fritzing sketch MyFlightControll (saved by Fritzing 0.9.3b)
breadboards: 1

parts:
  Bauteil3 = Arduino Nano (Rev3.0)
  BATT3 = LiPoly Battery (1300mAh)
  GY3 = MPU-6050 Board GY-521 [form="♀ (female)" package=THT]
  Part3 = Bluetooth HC-05 Macho
  J4 = FS-IA6 [form="♂ (shrouded male)" package=THT]
  M4 = ESC
  920KV_Motor4 = DJI 920 KV Motor
  M5 = ESC
  920KV_Motor5 = DJI 920 KV Motor
  M6 = ESC
  920KV_Motor6 = DJI 920 KV Motor
  M7 = ESC
  920KV_Motor7 = DJI 920 KV Motor
  R3 = Resistor [tolerance=±5% resistance=330 package=THT]
  LED3 = smd LED [color="Red (633nm)" package="0603 [SMD]"]
  R4 = Resistor [tolerance=±5% resistance=2.2k package=THT]
  R5 = Resistor [tolerance=±5% resistance=4.7k package=THT]

nets:
  N1: Bauteil3.D1/TX, R4.Pin_1, R5.Pin_1
  N2: Bauteil3.D0/RX, Part3.TXD
  GND: Bauteil3.GND, BATT3.negative, GY3.pin2, Part3.GND, J4.pin15, M4.GND, M5.GND, M6.GND, M7.GND, R3.Pin_1, R5.Pin_0
  N3: Bauteil3.D2, J4.pin4
  N4: Bauteil3.D3, M7.DATA
  N5: Bauteil3.D4, J4.pin5
  N6: Bauteil3.D5, J4.pin13
  N7: Bauteil3.D6, J4.pin3
  N8: Bauteil3.D7, J4.pin2
  N9: Bauteil3.D8, LED3.anode
  N10: Bauteil3.D9, M6.DATA
  N11: Bauteil3.D10, M5.DATA
  N12: Bauteil3.D11/MOSI, M4.DATA
  N13: Bauteil3.VIN, BATT3.positive
  5V: Bauteil3.5V, GY3.pin1, Part3.VCC, J4.pin12
  N14: Bauteil3.A5, GY3.pin3
  N15: Bauteil3.A4, GY3.pin4
  N16: Part3.RXD, R4.Pin_0
  N17: M4.U, 920KV_Motor4.u
  N18: M4.V, 920KV_Motor4.v
  N19: M4.W, 920KV_Motor4.w
  N20: M5.U, 920KV_Motor5.u
  N21: M5.V, 920KV_Motor5.v
  N22: M5.W, 920KV_Motor5.w
  N23: M6.U, 920KV_Motor6.u
  N24: M6.V, 920KV_Motor6.v
  N25: M6.W, 920KV_Motor6.w
  N26: M7.U, 920KV_Motor7.u
  N27: M7.V, 920KV_Motor7.v
  N28: M7.W, 920KV_Motor7.w
  N29: R3.Pin_0, LED3.cathode

notes:
  FL CW
  Front Left
  RR CW
  Rear Right
  FR CCW
  Front Right
  RL CCW
  Rear Left
  CH1 Pitch D5
  CH2 Roll D4
  CH3 Throttle D2
  CH4 Yaw D6
  CH5 Aux1 D7

custom parts:
  LiPoly Battery (1300mAh): Lithium Ion Polymer Battery (1300mAh)
  MPU-6050 Board GY-521: Acelerometro y Giroscopio MPU-6050 Board GY-521
  FS-IA6: FlySky FS-IA6 Receiver
  DJI 920 KV Motor: DJI Brushless Outrunner 2212/920K Motor F330-550
