# Fritzing sketch MyFlightControll2 (saved by Fritzing 0.9.3b)
breadboards: 1

parts:
  Bauteil3 = Arduino Nano (Rev3.0)
  BATT3 = LiPoly Battery (1300mAh)
  GY3 = MPU-6050 Board GY-521 [form="♀ (female)" package=THT]
  Part3 = Bluetooth HC-05 Macho
  J4 = FS-IA6 [form="♂ (shrouded male)" package=THT]  # not connected
  M4 = ESC
  920KV_Motor4 = DJI 920 KV Motor
  M5 = ESC
  920KV_Motor5 = DJI 920 KV Motor
  M6 = ESC
  920KV_Motor6 = DJI 920 KV Motor
  M7 = ESC
  920KV_Motor7 = DJI 920 KV Motor
  R3 = Resistor [tolerance=±5% resistance=330 package=THT]
  LED3 = smd LED [color="Red (633nm)" package="0603 [SMD]"]

nets:
  N1: Bauteil3.D1/TX, Part3.RXD
  N2: Bauteil3.D0/RX, Part3.TXD
  GND: Bauteil3.GND, BATT3.negative, GY3.pin2, Part3.GND, M4.GND, M5.GND, M6.GND, M7.GND, R3.Pin_1
  N3: Bauteil3.D3, M7.DATA
  N4: Bauteil3.D8, LED3.anode
  N5: Bauteil3.D9, M6.DATA
  N6: Bauteil3.D10, M5.DATA
  N7: Bauteil3.D11/MOSI, M4.DATA
  N8: Bauteil3.VIN, BATT3.positive
  5V: Bauteil3.5V, GY3.pin1, Part3.VCC
  N9: Bauteil3.A5, GY3.pin3
  N10: Bauteil3.A4, GY3.pin4
  N11: M4.U, 920KV_Motor4.u
  N12: M4.V, 920KV_Motor4.v
  N13: M4.W, 920KV_Motor4.w
  N14: M5.U, 920KV_Motor5.u
  N15: M5.V, 920KV_Motor5.v
  N16: M5.W, 920KV_Motor5.w
  N17: M6.U, 920KV_Motor6.u
  N18: M6.V, 920KV_Motor6.v
  N19: M6.W, 920KV_Motor6.w
  N20: M7.U, 920KV_Motor7.u
  N21: M7.V, 920KV_Motor7.v
  N22: M7.W, 920KV_Motor7.w
  N23: R3.Pin_0, LED3.cathode

custom parts:
  LiPoly Battery (1300mAh): Lithium Ion Polymer Battery (1300mAh)
  MPU-6050 Board GY-521: Acelerometro y Giroscopio MPU-6050 Board GY-521
  FS-IA6: FlySky FS-IA6 Receiver
  DJI 920 KV Motor: DJI Brushless Outrunner 2212/920K Motor F330-550
