# Fritzing sketch HC05-NAZE32Rev6 (saved by Fritzing 0.9.3b)
breadboards: 1

parts:
  Bauteil1 = Arduino Nano (Rev3.0) (ICSP)
  Part2 = Bluetooth HC-05 Macho
  R1 = Resistor [tolerance=±5% resistance=2.2k package="0805 [SMD]"]
  R2 = Resistor [tolerance=±5% resistance=4.7k package="0805 [SMD]"]

nets:
  GND: Bauteil1.GND, Part2.GND, R2.Pin_0
  N1: Bauteil1.D9, Part2.Key
  N2: Bauteil1.D10, Part2.TXD
  N3: Bauteil1.D11/MOSI, R1.Pin_0
  5V: Bauteil1.5V, Part2.VCC
  N4: Part2.RXD, R1.Pin_1, R2.Pin_1
